# Fritzing sketch wiring (saved by Fritzing 0.9.2b)
breadboards: 1

parts:
  パーツ2 = Arduino Wireless SD Shield
  S6 = Pushbutton [package="[THT]"]
  R5 = Resistor [tolerance=±5% resistance=1k package=THT]
  R6 = Resistor [tolerance=±5% resistance=1k package=THT]
  R7 = Resistor [tolerance=±5% resistance=1k package=THT]
  S7 = Pushbutton [package="[THT]"]
  S8 = Pushbutton [package="[THT]"]
  LED4 = RGB LED - (4 legs) [package="5 mm [THT]"]  # not connected

nets:
  N1: パーツ2.D10, S8.Pin_3, S8.Pin_4
  N2: パーツ2.D11, S7.Pin_3, S7.Pin_4
  N3: パーツ2.D12, S6.Pin_3, S6.Pin_4
  N4: パーツ2.D3, R6.Pin_1
  N5: パーツ2.D5, R5.Pin_1
  N6: パーツ2.D6, R7.Pin_1
  N7: パーツ2.GND, S6.Pin_1, S6.Pin_2, S7.Pin_1, S7.Pin_2, S8.Pin_1, S8.Pin_2

notes:
  Longest connects Yellow
